# Fritzing sketch pcb (saved by Fritzing 0.9.3b)
circuit board: 7cm x 5.2cm
breadboards: 1

parts:
  R1 = Resistor [tolerance=±5% resistance=100 package=THT]
  R4 = Resistor [tolerance=±5% resistance=10k package=THT]
  R3 = Resistor [tolerance=±5% resistance=100 package=THT]
  C3 = Electrolytic Capacitor [capacitance=1µF package="100 mil [THT, electrolytic]"]
  C4 = Electrolytic Capacitor [capacitance=1µF package="100 mil [THT, electrolytic]"]
  C5 = Electrolytic Capacitor [capacitance=1µF package="100 mil [THT, electrolytic]"]
  C6 = Electrolytic Capacitor [capacitance=1µF package="100 mil [THT, electrolytic]"]
  C7 = Electrolytic Capacitor [capacitance=1µF package="100 mil [THT, electrolytic]"]
  R5 = Resistor [tolerance=±5% resistance=200k package=THT]
  R6 = Resistor [tolerance=±5% resistance=100k package=THT]
  C8 = Electrolytic Capacitor [capacitance=10µF package="100 mil [THT, electrolytic]"]
  Pro_Micro = SparkFun Pro Micro [part_number=DEV-12640]
  J6 = female pin header, 4 pins [form="♀ (female)"]
  J7 = female pin header, 6 pins [form="♀ (female)"]
  J5 = female pin header, 1 pin [form="♀ (female)"]
  C9 = Electrolytic Capacitor [capacitance=10µF package="100 mil [THT, electrolytic]"]
  R13 = Resistor [tolerance=±5% resistance=100k package=THT]
  R14 = Resistor [tolerance=±5% resistance=200k package=THT]
  C10 = Electrolytic Capacitor [capacitance=10µF package="100 mil [THT, electrolytic]"]
  R7 = Resistor [tolerance=±5% resistance=1k package="1206 [SMD]"]
  R8 = Resistor [tolerance=±5% resistance=1k package="1206 [SMD]"]
  R10 = Resistor [tolerance=±5% resistance=1k package="1206 [SMD]"]
  R12 = Resistor [tolerance=±5% resistance=1k package="1206 [SMD]"]
  R2 = Resistor [tolerance=±5% resistance=10k package=THT]
  J1 = female pin header, 4 pins [form="♀ (female)"]
  J2 = female pin header, 4 pins [form="♀ (female)"]
  J4 = female pin header, 4 pins [form="♀ (female)"]
  J3 = female pin header, 4 pins [form="♀ (female)"]
  J12 = female pin header, 2 pins [form="♀ (female)"]
  D1 = Rectifier Diode [part_number=1N4001 package="300 mil [THT]"]
  R9 = Resistor [tolerance=±5% resistance=1k package="1206 [SMD]"]
  Q2 = NPN TO-220 [part_number=IRLB8721 package=TO-220]
  Q1 = NPN TO-220 [part_number=IRLB8721 package=TO-220]
  J13 = female pin header, 2 pins [form="♀ (female)"]
  J13_2 = female pin header, 2 pins [form="♀ (female)"]

nets:
  N1: R1.Pin_0, Pro_Micro.D6, R2.Pin_0
  N2: R1.Pin_1, Q1.Gate
  N3: R4.Pin_0, R3.Pin_0, Pro_Micro.D9
  GND: R4.Pin_1, C3.-, C4.-, C5.-, C6.-, C7.-, R6.Pin_1, C8.-, Pro_Micro.GND, C9.-, R13.Pin_1, C10.-, R2.Pin_1, J4.pin1, J4.pin2, J4.pin3, J4.pin4, Q2.Source, Q1.Source, J13.pin2, J13_2.pin2
  N4: R3.Pin_1, Q2.Gate
  N5: C3.+, Pro_Micro.MISO, R7.Pin_1, J1.pin1
  N6: C4.+, Pro_Micro.A1, R8.Pin_1, J1.pin2
  N7: C5.+, Pro_Micro.D7, J1.pin3, R9.Pin_1
  N8: C6.+, R14.Pin_0, J2.pin3
  N9: C7.+, Pro_Micro.SCK, R10.Pin_1, J1.pin4
  N10: R5.Pin_0, J2.pin2
  N11: R5.Pin_1, R6.Pin_0, C8.+, Pro_Micro.A0
  N12: Pro_Micro.RAW, C9.+, J2.pin4, J12.pin1, J13.pin1, J13_2.pin1
  N13: Pro_Micro.VCC, J12.pin2, D1.anode
  N14: Pro_Micro.A3, J6.pin4
  N15: Pro_Micro.A2, J6.pin3
  N16: Pro_Micro.MOSI, J6.pin2
  N17: Pro_Micro.D10, J6.pin1
  N18: Pro_Micro.D8, R13.Pin_0, R14.Pin_1, C10.+
  N19: Pro_Micro.D5, J7.pin1
  N20: Pro_Micro.D4, J7.pin2
  N21: Pro_Micro.D3, J7.pin3
  N22: Pro_Micro.D2, J7.pin4
  N23: Pro_Micro.RXI, J7.pin5
  N24: Pro_Micro.TXO, J7.pin6
  N25: J5.pin1, R12.Pin_1, J2.pin1
  N26: R7.Pin_0, R8.Pin_0, R10.Pin_0, R12.Pin_0, D1.cathode, R9.Pin_0
  N27: J3.pin1, J3.pin2, Q2.Drain
  N28: J3.pin3, J3.pin4, Q1.Drain

notes:
  GND
  LED1
  LED2
  sw1
  sw2
  sw3
  batt
  n/c
  sw4
  dome
  led2
  led1
  sw 1-4
  check this.. what is it for?
  batt monitor
  5  4 3  2  0  1
  1
  2
  10 16 20 21
  SprinterLights v6
  PWR
  RAW
  VCC

custom parts:
  SparkFun Pro Micro: This tiny little board does all of the neat-o Arduino tricks that you’re familiar with: 4 channels of 10-bit ADC, 5 PWM pins, 12 DIOs as well as hardware serial connections Rx and Tx. Running at 16MHz and 5V, this board will remind you a lot of your other favorite Arduino-compatible boards but this little guy can go just about anywhere. There is a voltage regulator on board so it can accept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
  NPN TO-220: NPN To-220
